# Fritzing sketch wiring (saved by Fritzing 0.9.0b)
breadboards: 1

parts:
  U1 = ESP8266 WiFi Module [part_number=ESP8266]
  DS1 = DS18B20 1-Wire Temperature Sensor [part_number=DS18B20]
  R1 = Resistor [tolerance=±5% resistance=220 package=THT]
  LED1 = LED - 5mm [color="Red (633nm)" package="5 mm [THT]"]
  R2 = Resistor [tolerance=±5% resistance=220 package=THT]
  VCC1 = Battery

nets:
  VCC: U1.VCC, U1.CH_PD, DS1.VDD, R1.Pin_0, R2.Pin_0, VCC1.+
  N1: U1.GPIO_0, LED1.cathode
  N2: U1.GPIO_2, DS1.DQ, R1.Pin_1
  GND: U1.GND, DS1.GND, VCC1.-
  N3: LED1.anode, R2.Pin_1

custom parts:
  ESP8266 WiFi Module: Generic WiFi Module based on the ESP8266 with onboard PCB antenna and UART communications
